// Logisim project seq_circuit.circ as structural Verilog: 1 circuit, main circuit main
module main (
  input  X,
  input  Y,
  input  in_3,
  input  in_4,
  output out_5,
  output Q_prime,
  output out_7,
  output Q_prime_2
);

  wire and_1_out, and_2_out, and_3_out, and_4_out, clock_1_out, clock_2_out, d_ff_1_q, nand_1_out,
       nand_2_out, nand_3_out, nand_4_out, nand_5_out, or_1_out, or_2_out, xor_1_out, xor_2_out;

  xor xor_1 (xor_1_out, X, Y);
  and and_1 (and_1_out, X, Y);
  xor xor_2 (xor_2_out, in_3, in_4);
  and and_2 (and_2_out, in_3, in_4);
  xor xor_3 (out_5, xor_1_out, nand_5_out);
  and and_3 (and_3_out, xor_1_out, nand_5_out);
  xor xor_4 (out_7, xor_2_out, d_ff_1_q);
  and and_4 (and_4_out, xor_2_out, d_ff_1_q);
  or or_1 (or_1_out, and_3_out, and_1_out);
  or or_2 (or_2_out, and_4_out, and_2_out);
  Clock clock_1 (.out(clock_1_out));
  Clock clock_2 (.out(clock_2_out));
  D_Flip_Flop d_ff_1 (.clk(clock_2_out), .D(or_2_out), .Q(d_ff_1_q), .Qn(Q_prime_2));  // open: preset, reset
  nand nand_1 (nand_1_out, nand_4_out, nand_2_out);
  nand nand_2 (nand_2_out, nand_1_out, clock_1_out);
  nand nand_3 (nand_3_out, nand_2_out, clock_1_out, nand_4_out);
  nand nand_4 (nand_4_out, nand_3_out, or_1_out);
  nand nand_5 (nand_5_out, nand_2_out, Q_prime);
  nand nand_6 (Q_prime, nand_5_out, nand_3_out);
endmodule
